// Logisim project 4-bitALU.circ as structural Verilog: 4 circuits, main circuit ALU
module ALU (
  input  f2,
  input  [3:0] A,
  input  f0,
  input  [3:0] B,
  input  f1,
  input  f3,
  output Cout,
  output [3:0] out_8
);

  wire n7_segment_display_1_p1, n7_segment_display_1_p2, n7_segment_display_2_p1, n7_segment_display_2_p2,
       n7_segment_display_5_p1, n7_segment_display_5_p2;
  wire [3:0] au_1_y1, lu_1_y2, multiplexer_1_out, multiplexer_2_out, not_1_out, not_2_out;

  // _7_Segment_Display 7_segment_display_1: pin names not known; wires that end beside it: n7_segment_display_1_p1, n7_segment_display_1_p2
  // BCD_to_7_Segment_decoder bcd_to_7_segment_decoder_1: pin names not known
  // Binary_to_BCD_converter #(.binvalue(4)) binary_to_bcd_converter_1: pin names not known; wires that end beside it: A, n7_segment_display_1_p1, n7_segment_display_1_p2
  // _7_Segment_Display 7_segment_display_2: pin names not known; wires that end beside it: n7_segment_display_2_p1, n7_segment_display_2_p2
  // BCD_to_7_Segment_decoder bcd_to_7_segment_decoder_2: pin names not known
  // Binary_to_BCD_converter #(.binvalue(4)) binary_to_bcd_converter_2: pin names not known; wires that end beside it: B, n7_segment_display_2_p1, n7_segment_display_2_p2
  _7_Segment_Display u_7_segment_display_3 ();  // open: g, f, a, b, e, d, c, dp
  // BCD_to_7_Segment_decoder bcd_to_7_segment_decoder_3: pin names not known
  _7_Segment_Display u_7_segment_display_4 ();  // open: g, f, a, b, e, d, c, dp
  // BCD_to_7_Segment_decoder bcd_to_7_segment_decoder_4: pin names not known
  assign not_1_out = ~A;  // NOT_Gate not_1, 4 bits wide
  assign not_2_out = ~B;  // NOT_Gate not_2, 4 bits wide
  Multiplexer #(.width(4)) multiplexer_1 (.in0(A), .in1(not_1_out), .out(multiplexer_1_out), .sel(f0));
  Multiplexer #(.width(4)) multiplexer_2 (.in0(B), .in1(not_2_out), .out(multiplexer_2_out), .sel(f1));
  AU au_1 (.Cin(f2), .A(multiplexer_1_out), .B(multiplexer_2_out), .y1(au_1_y1), .E(Cout));
  LU lu_1 (.A(A), .B(multiplexer_2_out), .S1(f0), .S0(f2), .Y2(lu_1_y2));
  Multiplexer #(.width(4)) multiplexer_3 (.in0(au_1_y1), .in1(lu_1_y2), .out(out_8), .sel(f3));
  // _7_Segment_Display 7_segment_display_5: pin names not known; wires that end beside it: n7_segment_display_5_p1, n7_segment_display_5_p2
  _7_Segment_Display u_7_segment_display_6 ();  // open: g, f, a, b, e, d, c, dp
  // BCD_to_7_Segment_decoder bcd_to_7_segment_decoder_5: pin names not known
  // BCD_to_7_Segment_decoder bcd_to_7_segment_decoder_6: pin names not known
  // Binary_to_BCD_converter #(.binvalue(4)) binary_to_bcd_converter_3: pin names not known; wires that end beside it: out_8, n7_segment_display_5_p1, n7_segment_display_5_p2
endmodule

module AU (
  input  Cin,
  input  [3:0] A,
  input  [3:0] B,
  output [3:0] y1,
  output E
);

  Adder #(.width(4)) adder_1 (.a(A), .b(B), .out(y1), .cin(Cin), .cout(E));
endmodule

module LU (
  input  [3:0] A,
  input  [3:0] B,
  input  S1,
  input  S0,
  output [3:0] Y2
);

  wire [3:0] and_1_out, or_1_out, xor_1_out;

  assign or_1_out = A | B;  // OR_Gate or_1, 4 bits wide
  assign and_1_out = A & B;  // AND_Gate and_1, 4 bits wide
  assign xor_1_out = A ^ B;  // XOR_Gate xor_1, 4 bits wide
  Multiplexer #(.select(2), .width(4)) multiplexer_1 (
    .in0(or_1_out), .in1(and_1_out), .in2(xor_1_out), .in3(B), .out(Y2), .sel({S1, S0}));
endmodule

module cascading (
  input  [7:0] in_1,
  input  [7:0] in_2,
  input  f0,
  input  f1,
  input  f3,
  input  f2,
  output [7:0] out_7
);

  wire alu_1_cout;

  ALU alu_1 (.f2(f2), .A(in_1[3:0]), .f0(f0), .B(in_2[3:0]), .f1(f1), .f3(f3), .Cout(alu_1_cout), .out_8(out_7[3:0]));
  ALU alu_2 (
    .f2(alu_1_cout), .A(in_1[7:4]), .f0(f0), .B(in_2[7:4]), .f1(f1), .f3(f3), .out_8(out_7[7:4]));  // open: Cout
endmodule
