// Logisim project 4bit_add_shift_multiplier.circ as structural Verilog: 3 circuits, main circuit UNIVERAL_REGISTER
module UNIVERAL_REGISTER (
  input  SR,
  input  SL,
  input  S1,
  input  I3,
  input  S0,
  input  I2,
  input  I1,
  input  I0,
  output Q3,
  output Q2,
  output Q1,
  output Q0,
  output OP_R,
  output OP_L
);

  wire CLK_out, multiplexer_2_out, multiplexer_3_out, multiplexer_4_out;

  Clock CLK (.out(CLK_out));
  D_Flip_Flop #(.trigger("falling")) d_ff_1 (.D(OP_L), .clk(CLK_out), .Q(Q3));  // open: Qn, preset, reset
  Multiplexer #(.select(2)) multiplexer_1 (.in0(Q3), .in1(Q2), .in2(SR), .in3(I3), .out(OP_L), .sel({S1, S0}));
  D_Flip_Flop #(.trigger("falling")) d_ff_2 (.D(multiplexer_2_out), .clk(CLK_out), .Q(Q2));  // open: Qn, preset, reset
  Multiplexer #(.select(2)) multiplexer_2 (
    .in0(Q2), .in1(Q1), .in2(Q3), .in3(I2), .out(multiplexer_2_out), .sel({S1, S0}));
  D_Flip_Flop #(.trigger("falling")) d_ff_3 (.D(multiplexer_3_out), .clk(CLK_out), .Q(Q1));  // open: Qn, preset, reset
  Multiplexer #(.select(2)) multiplexer_3 (
    .in0(Q1), .in1(OP_R), .in2(Q2), .in3(I1), .out(multiplexer_3_out), .sel({S1, S0}));
  D_Flip_Flop #(.trigger("falling")) d_ff_4 (
    .D(multiplexer_4_out), .clk(CLK_out), .Q(OP_R));  // open: Qn, preset, reset
  Multiplexer #(.select(2)) multiplexer_4 (
    .in0(OP_R), .in1(SL), .in2(Q1), .in3(I0), .out(multiplexer_4_out), .sel({S1, S0}));

  assign Q0 = OP_R;

  // Notes on the sheet:
  //   SO  S1
  //   0    0
  //   0   1
  //   1  0
  //   1   1
  //   TRUTH TABLE
  //   MODE
  //   STORAGE
  //   LEFT SHIFT
  //   RIGHT SHIFT
  //   PARALLEL LOAD
endmodule

module MULTIPLER (
  input  [3:0] A,
  input  [3:0] B
);

  wire ACCUMULATOR_op_r, adder_1_cout, CARRY_q, clock_1_out, cu_1_y0, cu_1_y1, cu_1_y2, cu_1_y3, M_op_r,
       n7_segment_display_1_p1, n7_segment_display_1_p2, n7_segment_display_2_p2;
  wire [3:0] adder_1_out, binary_to_bcd_converter_1_p1, binary_to_bcd_converter_1_p1_2, multiplexer_1_out;

  Clock clock_1 (.out(clock_1_out));
  Adder #(.width(4)) adder_1 (
    .a(binary_to_bcd_converter_1_p1_2), .b(multiplexer_1_out), .out(adder_1_out), .cout(adder_1_cout));  // open: cin
  // _7_Segment_Display 7_segment_display_1: pin names not known; wires that end beside it: n7_segment_display_1_p1, n7_segment_display_1_p2
  // BCD_to_7_Segment_decoder bcd_to_7_segment_decoder_1: pin names not known
  // _7_Segment_Display 7_segment_display_2: pin names not known; wires that end beside it: n7_segment_display_1_p2, n7_segment_display_2_p2
  _7_Segment_Display u_7_segment_display_3 ();  // open: g, f, a, b, e, d, c, dp
  // BCD_to_7_Segment_decoder bcd_to_7_segment_decoder_2: pin names not known
  // BCD_to_7_Segment_decoder bcd_to_7_segment_decoder_3: pin names not known
  D_Flip_Flop #(.trigger("falling")) CARRY (
    .D(adder_1_cout), .clk(clock_1_out), .Q(CARRY_q));  // open: Qn, preset, reset
  Multiplexer #(.width(4)) multiplexer_1 (
    .in0(4'b0000), .in1(B), .out(multiplexer_1_out), .sel(binary_to_bcd_converter_1_p1[0]));
  // Binary_to_BCD_converter #(.binvalue(8)) binary_to_bcd_converter_1: pin names not known; wires that end beside it: {binary_to_bcd_converter_1_p1_2, binary_to_bcd_converter_1_p1}, n7_segment_display_1_p1, adder_1_out[2], n7_segment_display_1_p2, n7_segment_display_2_p2
  UNIVERAL_REGISTER ACCUMULATOR (
    .SR(CARRY_q), .S1(cu_1_y2), .I3(adder_1_out[3]), .S0(cu_1_y3), .I2(adder_1_out[2]), .I1(adder_1_out[1]),
    .I0(adder_1_out[0]), .Q3(binary_to_bcd_converter_1_p1_2[3]), .Q2(binary_to_bcd_converter_1_p1_2[2]),
    .Q1(binary_to_bcd_converter_1_p1_2[1]), .Q0(binary_to_bcd_converter_1_p1_2[0]), .OP_R(ACCUMULATOR_op_r));  // open: SL, OP_L
  CU cu_1 (.Y3(cu_1_y3), .Y2(cu_1_y2), .Y1(cu_1_y1), .Y0(cu_1_y0));
  UNIVERAL_REGISTER M (
    .SR(ACCUMULATOR_op_r), .S1(cu_1_y0), .I3(A[3]), .S0(cu_1_y1), .I2(A[2]), .I1(A[1]), .I0(A[0]),
    .Q3(binary_to_bcd_converter_1_p1[3]), .Q2(binary_to_bcd_converter_1_p1[2]),
    .Q1(binary_to_bcd_converter_1_p1[1]), .Q0(binary_to_bcd_converter_1_p1[0]), .OP_R(M_op_r));  // open: SL, OP_L
endmodule

module CU (
  output Y3,
  output Y2,
  output Y1,
  output Y0
);

  wire and_1_out, and_2_out, and_3_out, and_4_out, and_5_out, and_6_out, and_7_out, and_8_out, and_9_out,
       and_11_out, and_12_out, clock_1_out, d_ff_1_q, d_ff_1_qn, d_ff_2_q, d_ff_2_qn, d_ff_3_q, d_ff_3_qn,
       d_ff_4_q, d_ff_4_qn, not_1_out, not_2_out, not_3_out, not_4_out, or_1_out, or_2_out, or_3_out,
       or_4_out;

  not not_1 (not_1_out, d_ff_1_q);
  not not_2 (not_2_out, d_ff_2_q);
  not not_3 (not_3_out, d_ff_3_q);
  not not_4 (not_4_out, d_ff_4_q);
  and and_1 (and_1_out, d_ff_2_q, d_ff_3_q, d_ff_4_q);
  and and_2 (and_2_out, not_1_out, not_2_out, d_ff_3_q, d_ff_4_q);
  and and_3 (and_3_out, not_1_out, d_ff_2_q, not_3_out);
  and and_4 (and_4_out, not_1_out, d_ff_2_q, not_4_out);
  and and_5 (and_5_out, not_1_out, not_3_out, d_ff_4_q);
  and and_6 (and_6_out, not_1_out, d_ff_3_q, not_4_out);
  or or_1 (or_1_out, not_4_out, d_ff_1_q);
  or or_2 (or_2_out, and_1_out, d_ff_1_q);
  or or_3 (or_3_out, and_2_out, and_3_out, and_4_out);
  or or_4 (or_4_out, and_5_out, and_6_out);
  D_Flip_Flop #(.trigger("falling")) d_ff_1 (
    .D(or_2_out), .clk(clock_1_out), .Q(d_ff_1_q), .Qn(d_ff_1_qn));  // open: preset, reset
  D_Flip_Flop #(.trigger("falling")) d_ff_2 (
    .D(or_3_out), .clk(clock_1_out), .Q(d_ff_2_q), .Qn(d_ff_2_qn));  // open: preset, reset
  Clock clock_1 (.out(clock_1_out));
  D_Flip_Flop #(.trigger("falling")) d_ff_3 (
    .D(or_4_out), .clk(clock_1_out), .Q(d_ff_3_q), .Qn(d_ff_3_qn));  // open: preset, reset
  D_Flip_Flop #(.trigger("falling")) d_ff_4 (
    .D(or_1_out), .clk(clock_1_out), .Q(d_ff_4_q), .Qn(d_ff_4_qn));  // open: preset, reset
  and and_7 (and_7_out, d_ff_1_qn, d_ff_4_q);
  and and_8 (and_8_out, d_ff_1_qn, d_ff_2_qn, d_ff_3_qn);
  and and_9 (and_9_out, d_ff_2_qn, d_ff_3_qn, d_ff_4_qn);
  and and_10 (Y1, d_ff_1_qn, d_ff_2_qn, d_ff_3_qn, d_ff_4_qn);
  and and_11 (and_11_out, d_ff_1_qn, d_ff_4_qn);
  and and_12 (and_12_out, d_ff_2_qn, d_ff_3_qn, d_ff_4_qn);
  or or_5 (Y3, and_7_out, and_8_out);
  or or_6 (Y2, d_ff_1_qn, and_9_out);
  or or_7 (Y0, and_11_out, and_12_out);
endmodule
