// Logisim project 4bit_multiplier.circ as structural Verilog: 1 circuit, main circuit main
module main (
  input  [3:0] A,
  input  [3:0] B
);

  wire adder_2_cout, adder_2_out, adder_3_cout, adder_4_cout, adder_4_out, adder_5_cout, adder_5_out,
       adder_6_cout, adder_7_cout, adder_7_out, adder_8_cout, adder_8_out, adder_9_cout, adder_10_cout,
       adder_10_out, adder_11_cout, adder_12_cout, and_1_out, and_2_out, and_3_out, and_4_out, and_5_out,
       and_6_out, and_7_out, and_8_out, and_9_out, and_10_out, and_11_out, and_12_out, and_13_out,
       and_14_out, and_15_out, binary_to_bcd_converter_1_p4, n7_segment_display_1_p1,
       n7_segment_display_1_p2, n7_segment_display_4_p1, n7_segment_display_4_p2, n7_segment_display_5_p1,
       n7_segment_display_5_p2;
  wire [7:0] binary_to_bcd_converter_1_p1;

  and and_1 (and_1_out, A[3], B[3]);
  Adder #(.width(1)) adder_1 (
    .a(and_1_out), .b(adder_2_cout), .out(binary_to_bcd_converter_1_p1[6]), .cin(adder_3_cout),
    .cout(binary_to_bcd_converter_1_p1[7]));
  and and_2 (and_2_out, A[3], B[2]);
  Adder #(.width(1)) adder_2 (
    .a(and_2_out), .b(adder_4_cout), .out(adder_2_out), .cin(adder_5_cout), .cout(adder_2_cout));
  and and_3 (and_3_out, A[2], B[3]);
  Adder #(.width(1)) adder_3 (
    .a(and_3_out), .b(adder_2_out), .out(binary_to_bcd_converter_1_p1[5]), .cin(adder_6_cout),
    .cout(adder_3_cout));
  // _7_Segment_Display 7_segment_display_1: pin names not known; wires that end beside it: n7_segment_display_1_p1, n7_segment_display_1_p2
  // BCD_to_7_Segment_decoder bcd_to_7_segment_decoder_1: pin names not known
  // Binary_to_BCD_converter #(.binvalue(8)) binary_to_bcd_converter_1: pin names not known; wires that end beside it: binary_to_bcd_converter_1_p1, n7_segment_display_1_p1, n7_segment_display_1_p2, binary_to_bcd_converter_1_p4
  and and_4 (and_4_out, A[3], B[1]);
  Adder #(.width(1)) adder_4 (.a(and_4_out), .b(adder_7_cout), .out(adder_4_out), .cout(adder_4_cout));  // open: cin
  and and_5 (and_5_out, A[2], B[2]);
  Adder #(.width(1)) adder_5 (
    .a(and_5_out), .b(adder_4_out), .out(adder_5_out), .cin(adder_8_cout), .cout(adder_5_cout));
  and and_6 (and_6_out, A[1], B[3]);
  Adder #(.width(1)) adder_6 (
    .a(and_6_out), .b(adder_5_out), .out(binary_to_bcd_converter_1_p1[4]), .cin(adder_9_cout),
    .cout(adder_6_cout));
  // _7_Segment_Display 7_segment_display_2: pin names not known; wires that end beside it: n7_segment_display_1_p2, binary_to_bcd_converter_1_p4
  // BCD_to_7_Segment_decoder bcd_to_7_segment_decoder_2: pin names not known
  and and_7 (and_7_out, A[3], B[0]);
  and and_8 (and_8_out, A[2], B[1]);
  Adder #(.width(1)) adder_7 (
    .a(and_8_out), .b(and_7_out), .out(adder_7_out), .cin(adder_10_cout), .cout(adder_7_cout));
  and and_9 (and_9_out, A[1], B[2]);
  Adder #(.width(1)) adder_8 (
    .a(and_9_out), .b(adder_7_out), .out(adder_8_out), .cin(adder_11_cout), .cout(adder_8_cout));
  and and_10 (and_10_out, A[0], B[3]);
  _7_Segment_Display u_7_segment_display_3 ();  // open: g, f, a, b, e, d, c, dp
  // BCD_to_7_Segment_decoder bcd_to_7_segment_decoder_3: pin names not known
  Adder #(.width(1)) adder_9 (
    .a(adder_8_out), .b(and_10_out), .out(binary_to_bcd_converter_1_p1[3]), .cout(adder_9_cout));  // open: cin
  and and_11 (and_11_out, A[2], B[0]);
  and and_12 (and_12_out, A[1], B[1]);
  Adder #(.width(1)) adder_10 (
    .a(and_12_out), .b(and_11_out), .out(adder_10_out), .cin(adder_12_cout), .cout(adder_10_cout));
  and and_13 (and_13_out, A[0], B[2]);
  Adder #(.width(1)) adder_11 (
    .a(adder_10_out), .b(and_13_out), .out(binary_to_bcd_converter_1_p1[2]), .cout(adder_11_cout));  // open: cin
  and and_14 (and_14_out, A[1], B[0]);
  and and_15 (and_15_out, A[0], B[1]);
  Adder #(.width(1)) adder_12 (
    .a(and_14_out), .b(and_15_out), .out(binary_to_bcd_converter_1_p1[1]), .cout(adder_12_cout));  // open: cin
  and and_16 (binary_to_bcd_converter_1_p1[0], A[0], B[0]);
  // _7_Segment_Display 7_segment_display_4: pin names not known; wires that end beside it: n7_segment_display_4_p1, n7_segment_display_4_p2
  // BCD_to_7_Segment_decoder bcd_to_7_segment_decoder_4: pin names not known
  // Binary_to_BCD_converter #(.binvalue(4)) binary_to_bcd_converter_2: pin names not known; wires that end beside it: A, n7_segment_display_4_p1, n7_segment_display_4_p2
  // _7_Segment_Display 7_segment_display_5: pin names not known; wires that end beside it: n7_segment_display_5_p1, n7_segment_display_5_p2
  _7_Segment_Display u_7_segment_display_6 ();  // open: g, f, a, b, e, d, c, dp
  // BCD_to_7_Segment_decoder bcd_to_7_segment_decoder_5: pin names not known
  // BCD_to_7_Segment_decoder bcd_to_7_segment_decoder_6: pin names not known
  // Binary_to_BCD_converter #(.binvalue(4)) binary_to_bcd_converter_3: pin names not known; wires that end beside it: B, n7_segment_display_5_p1, n7_segment_display_5_p2
  _7_Segment_Display u_7_segment_display_7 ();  // open: g, f, a, b, e, d, c, dp
  // BCD_to_7_Segment_decoder bcd_to_7_segment_decoder_7: pin names not known
endmodule
