// Logisim project custom_sequence_counter.circ as structural Verilog: 1 circuit, main circuit main
module main (
);

  wire and_1_out, and_2_out, and_3_out, and_4_out, and_5_out, and_6_out, and_7_out, and_8_out, and_9_out,
       and_10_out, and_11_out, and_12_out, and_13_out, and_14_out, and_15_out, and_16_out, and_17_out,
       bcd_to_7_segment_decoder_2_p1, clock_1_out, d_ff_1_qn, d_ff_2_qn, d_ff_4_qn, n7_segment_display_1_p1,
       n7_segment_display_1_p2, or_1_out, or_2_out, or_3_out, or_4_out;
  wire [3:0] binary_to_bcd_converter_1_p1;

  and and_1 (and_1_out, d_ff_1_qn, bcd_to_7_segment_decoder_2_p1, d_ff_4_qn);
  and and_2 (and_2_out, d_ff_1_qn, binary_to_bcd_converter_1_p1[2]);
  and and_3 (and_3_out, binary_to_bcd_converter_1_p1[2], d_ff_4_qn);
  and and_4 (and_4_out, binary_to_bcd_converter_1_p1[2], binary_to_bcd_converter_1_p1[1]);
  and and_5 (and_5_out, d_ff_1_qn, d_ff_2_qn, bcd_to_7_segment_decoder_2_p1);
  and and_6 (and_6_out, d_ff_1_qn, d_ff_2_qn, binary_to_bcd_converter_1_p1[0]);
  and and_7 (and_7_out, bcd_to_7_segment_decoder_2_p1, binary_to_bcd_converter_1_p1[0]);
  and and_8 (and_8_out, binary_to_bcd_converter_1_p1[3], binary_to_bcd_converter_1_p1[2], bcd_to_7_segment_decoder_2_p1);
  and and_9 (and_9_out, binary_to_bcd_converter_1_p1[3], binary_to_bcd_converter_1_p1[2], binary_to_bcd_converter_1_p1[0]);
  and and_10 (and_10_out, d_ff_2_qn, bcd_to_7_segment_decoder_2_p1, d_ff_4_qn);
  and and_11 (and_11_out, binary_to_bcd_converter_1_p1[2], binary_to_bcd_converter_1_p1[1], d_ff_4_qn);
  and and_12 (and_12_out, binary_to_bcd_converter_1_p1[3], binary_to_bcd_converter_1_p1[0]);
  and and_13 (and_13_out, d_ff_1_qn, bcd_to_7_segment_decoder_2_p1, d_ff_4_qn);
  and and_14 (and_14_out, d_ff_2_qn, binary_to_bcd_converter_1_p1[1], binary_to_bcd_converter_1_p1[0]);
  and and_15 (and_15_out, binary_to_bcd_converter_1_p1[3], d_ff_2_qn, binary_to_bcd_converter_1_p1[0]);
  and and_16 (and_16_out, binary_to_bcd_converter_1_p1[3], binary_to_bcd_converter_1_p1[1], d_ff_4_qn);
  and and_17 (and_17_out, binary_to_bcd_converter_1_p1[3], binary_to_bcd_converter_1_p1[2], d_ff_4_qn);
  or or_1 (or_1_out, and_1_out, and_2_out, and_3_out, and_4_out);
  or or_2 (or_2_out, and_5_out, and_6_out, and_7_out, and_8_out, and_9_out);
  or or_3 (or_3_out, and_10_out, and_11_out, and_12_out);
  or or_4 (or_4_out, and_13_out, and_14_out, and_15_out, and_16_out, and_17_out);
  D_Flip_Flop d_ff_1 (
    .D(or_1_out), .clk(clock_1_out), .Q(binary_to_bcd_converter_1_p1[3]), .Qn(d_ff_1_qn));  // open: preset, reset
  Clock clock_1 (.out(clock_1_out));
  // _7_Segment_Display 7_segment_display_1: pin names not known; wires that end beside it: n7_segment_display_1_p1, n7_segment_display_1_p2
  // BCD_to_7_Segment_decoder bcd_to_7_segment_decoder_1: pin names not known; wires that end beside it: or_1_out
  // Binary_to_BCD_converter #(.binvalue(4)) binary_to_bcd_converter_1: pin names not known; wires that end beside it: binary_to_bcd_converter_1_p1, n7_segment_display_1_p1, n7_segment_display_1_p2
  D_Flip_Flop d_ff_2 (
    .D(or_2_out), .clk(clock_1_out), .Q(binary_to_bcd_converter_1_p1[2]), .Qn(d_ff_2_qn));  // open: preset, reset
  _7_Segment_Display u_7_segment_display_2 ();  // open: g, f, a, b, e, d, c, dp
  // BCD_to_7_Segment_decoder bcd_to_7_segment_decoder_2: pin names not known; wires that end beside it: bcd_to_7_segment_decoder_2_p1
  D_Flip_Flop d_ff_3 (
    .D(or_3_out), .clk(clock_1_out), .Q(binary_to_bcd_converter_1_p1[1]), .Qn(bcd_to_7_segment_decoder_2_p1));  // open: preset, reset
  D_Flip_Flop d_ff_4 (
    .D(or_4_out), .clk(clock_1_out), .Q(binary_to_bcd_converter_1_p1[0]), .Qn(d_ff_4_qn));  // open: preset, reset
endmodule
