// Logisim project UNIVERSAL_SHIFT_REGISTER.circ as structural Verilog: 1 circuit, main circuit main
module main (
  input  SR,
  input  SL,
  input  S1,
  input  I3,
  input  S0,
  input  I2,
  input  I1,
  input  I0
);

  wire clock_1_out, d_ff_1_q, d_ff_2_q, d_ff_3_q, d_ff_4_q, multiplexer_1_out, multiplexer_2_out,
       multiplexer_3_out, multiplexer_4_out;

  Clock clock_1 (.out(clock_1_out));
  D_Flip_Flop d_ff_1 (.D(multiplexer_1_out), .clk(clock_1_out), .Q(d_ff_1_q));  // open: Qn, preset, reset
  Multiplexer #(.select(2)) multiplexer_1 (
    .in0(d_ff_1_q), .in1(d_ff_2_q), .in2(SR), .in3(I3), .out(multiplexer_1_out), .sel({S1, S0}));
  D_Flip_Flop d_ff_2 (.D(multiplexer_2_out), .clk(clock_1_out), .Q(d_ff_2_q));  // open: Qn, preset, reset
  Multiplexer #(.select(2)) multiplexer_2 (
    .in0(d_ff_2_q), .in1(d_ff_3_q), .in2(d_ff_1_q), .in3(I2), .out(multiplexer_2_out), .sel({S1, S0}));
  D_Flip_Flop d_ff_3 (.D(multiplexer_3_out), .clk(clock_1_out), .Q(d_ff_3_q));  // open: Qn, preset, reset
  Multiplexer #(.select(2)) multiplexer_3 (
    .in0(d_ff_3_q), .in1(d_ff_4_q), .in2(d_ff_2_q), .in3(I1), .out(multiplexer_3_out), .sel({S1, S0}));
  D_Flip_Flop d_ff_4 (.D(multiplexer_4_out), .clk(clock_1_out), .Q(d_ff_4_q));  // open: Qn, preset, reset
  Multiplexer #(.select(2)) multiplexer_4 (
    .in0(d_ff_4_q), .in1(SL), .in2(d_ff_3_q), .in3(I0), .out(multiplexer_4_out), .sel({S1, S0}));

  // Notes on the sheet:
  //   TRUTH TABLE
  //   SO  S1
  //   0    0
  //   0   1
  //   1  0
  //   1   1
  //   MODE
  //   STORAGE
  //   LEFT SHIFT
  //   RIGHT SHIFT
  //   PARALLEL LOAD
endmodule
